# Fritzing sketch NODEMCU WITH SENSOR ANDMOTORS (saved by Fritzing 0.9.3b)

parts:
  M1 = fc-51 [package=THT]
  M2 = fc-51 [package=THT]
  U1 = ESP8266 NodeMCU LoLin module
  LED1 = smd LED [color="Red (633nm)" package="0603 [SMD]"]  # not connected
  LED2 = smd LED [color="Red (633nm)" package="0603 [SMD]"]
  R1 = Resistor [tolerance=±5% resistance=220 package=THT]
  R2 = Resistor [tolerance=±5% resistance=220 package=THT]
  BAT1 = BC9VPC [package=bc9vpc]
  J2 = Basic Servo
  J1 = Basic Servo
  J3 = Piezo Speaker  # not connected

nets:
  N1: M1.pin1, U1.D7
  N2: M1.pin3, M2.pin3
  N3: M2.pin2, LED2.anode
  N4: U1.D1, J2.pulse
  N5: U1.D3, R2.Pin_1
  N6: U1.D5, R1.Pin_1
  N7: U1.D8, J1.pulse
  N8: BAT1.V+, J1.vcc
  N9: BAT1.V-, J2.gnd

custom parts:
  ESP8266 NodeMCU LoLin module: ESP8266 based NodeMCU
